# Fritzing sketch arduino_stoplight_v2 (saved by Fritzing 0.9.10b)
breadboards: 1

parts:
  Part1 = Arduino Uno (Rev3)
  LED1 = LED - 5mm [color="Red (633nm)" current=0.030 package="5 mm [THT]"]
  LED2 = LED - 5mm [color="Yellow (595nm)" current=0.030 package="5 mm [THT]"]
  LED3 = LED - 5mm [color="Green (565nm)" current=0.030 package="5 mm [THT]"]
  LED4 = LED - 5mm [color="Blue (430nm)" current=0.030 package="5 mm [THT]"]
  R1 = Resistor [tolerance=±5% power=0.25 resistance=220 package=THT]
  R2 = Resistor [tolerance=±5% power=0.25 resistance=220 package=THT]
  R3 = Resistor [tolerance=±5% power=0.25 resistance=220 package=THT]
  R4 = Resistor [tolerance=±5% power=0.25 resistance=220 package=THT]
  Part2 = Bluetooth HC-05 Macho
  R5 = Resistor [tolerance=±5% power=0.25 resistance=1k package=THT]
  R6 = Resistor [tolerance=±5% power=0.25 resistance=2.2k package=THT]

nets:
  GND: Part1.GND, LED1.cathode, LED2.cathode, LED3.cathode, LED4.cathode, Part2.GND, R6.Pin_0
  N1: Part1.D0/RX, Part2.TXD
  N2: Part1.D4, R1.Pin_1
  N3: Part1.D5_PWM, R2.Pin_1
  N4: Part1.D6_PWM, R3.Pin_1
  N5: Part1.D7, R4.Pin_1
  5V: Part1.5V, Part2.VCC
  N6: LED1.anode, R4.Pin_0
  N7: LED2.anode, R3.Pin_0
  N8: LED3.anode, R2.Pin_0
  N9: LED4.anode, R1.Pin_0
  N10: Part2.RXD, R5.Pin_0, R6.Pin_1
